// Logisim project ULA.circ as structural Verilog: 4 circuits, main circuit main
module main (
  input  A,
  input  B,
  output out_3
);

  or or_1 (out_3, A, B);
endmodule

module half_adder (
  input  A,
  input  B,
  output Carry_out,
  output Soma
);

  and and_1 (Carry_out, B, A);
  xor xor_1 (Soma, A, B);
endmodule

module full_adder (
  input  A,
  input  B,
  input  Carry_in,
  output Carry_out,
  output Soma
);

  wire half_adder_2_carry_out, half_adder_carry_out, half_adder_soma;

  half_adder half_adder (.A(A), .B(B), .Carry_out(half_adder_carry_out), .Soma(half_adder_soma));
  half_adder half_adder_2 (.A(half_adder_soma), .B(Carry_in), .Carry_out(half_adder_2_carry_out), .Soma(Soma));
  or or_1 (Carry_out, half_adder_carry_out, half_adder_2_carry_out);
endmodule

module C2_format (
  input  M,
  input  D1,
  input  D2,
  input  D3,
  input  D4,
  input  D5,
  input  in_7,
  output out_8,
  output out_9,
  output out_10,
  output out_11,
  output out_12
);

  wire full_adder_1_carry_out, full_adder_2_carry_out, full_adder_3_carry_out, full_adder_4_carry_out,
       not_1_out, not_2_out, not_3_out, not_4_out, not_5_out, not_6_out, xor_1_out, xor_2_out, xor_3_out,
       xor_4_out, xor_5_out;

  not not_1 (not_1_out, D1);
  not not_2 (not_2_out, D2);
  not not_3 (not_3_out, D3);
  not not_4 (not_4_out, D4);
  not not_5 (not_5_out, D5);
  not not_6 (not_6_out, M);
  xor xor_1 (xor_1_out, not_1_out, M);
  xor xor_2 (xor_2_out, not_2_out, M);
  xor xor_3 (xor_3_out, not_3_out, M);
  xor xor_4 (xor_4_out, not_4_out, M);
  xor xor_5 (xor_5_out, not_5_out, M);
  full_adder full_adder_1 (
    .A(xor_1_out), .B(not_6_out), .Carry_in(in_7), .Carry_out(full_adder_1_carry_out), .Soma(out_8));
  full_adder full_adder_2 (
    .A(xor_2_out), .B(in_7), .Carry_in(full_adder_1_carry_out), .Carry_out(full_adder_2_carry_out),
    .Soma(out_9));
  full_adder full_adder_3 (
    .A(xor_3_out), .B(in_7), .Carry_in(full_adder_2_carry_out), .Carry_out(full_adder_3_carry_out),
    .Soma(out_10));
  full_adder full_adder_4 (
    .A(xor_4_out), .B(in_7), .Carry_in(full_adder_3_carry_out), .Carry_out(full_adder_4_carry_out),
    .Soma(out_11));
  full_adder full_adder_5 (
    .A(xor_5_out), .B(in_7), .Carry_in(full_adder_4_carry_out), .Soma(out_12));  // open: Carry_out
endmodule
